# Fritzing sketch pcb (saved by Fritzing 0.9.3b)
circuit board: 5.08cm x 5.08cm
breadboards: 1

parts:
  MCP3008 = IC, DIP package, 16 pins [chip_label=MCP3008]
  R3 = Resistor [tolerance=±5% resistance=470 package=THT]
  LED = LED - 3mm [color="Red (633nm)" package="3 mm [THT]"]
  Grove1 = Sound Sensor
  Grove2 = Grove Light Sensor
  Header = Generic double row rounded female header - 26 pins [form="♀ (female rounded)" package=THT]

nets:
  N1: MCP3008.pin1, Grove2.SIG
  N2: MCP3008.pin2, Grove1.SIG
  GND: MCP3008.pin9, MCP3008.pin14, R3.Pin_0, Grove1.GND, Grove2.GND, Header.pin24
  N3: MCP3008.pin10, Header.pin15
  N4: MCP3008.pin11, Header.pin10
  N5: MCP3008.pin12, Header.pin11
  N6: MCP3008.pin13, Header.pin12
  VCC: MCP3008.pin15, MCP3008.pin16, Grove1.VCC, Grove2.VCC, Header.pin1
  N7: R3.Pin_1, LED.cathode
  N8: LED.anode, Header.pin6

notes:
  June and Claire

custom parts:
  Sound Sensor: Grove - Sound Sensor can detect the sound strength of the environment.
  Generic double row rounded female header - 26 pins: Generic double row rounded female header
